# Fritzing sketch wiring (saved by Fritzing 0.9.3b)

parts:
  WeMos_D1_Mini1 = WeMos D1 Mini  # not connected
  WeMos_D1_Mini_OLED_Shield1 = WeMos D1 Mini OLED Shield
  Part1 = Adafruit ADS1115 16Bit I2C ADC [part_number="Adafruit #1085"]
  Part2 = Thumb Joystick

nets:
  3V3: WeMos_D1_Mini_OLED_Shield1.3V3, Part1.VDD
  N1: WeMos_D1_Mini_OLED_Shield1.D1, Part1.SCL
  N2: WeMos_D1_Mini_OLED_Shield1.D2, Part1.SDA
  N3: WeMos_D1_Mini_OLED_Shield1.G, Part1.GND
  N4: Part1.AIN2, Part2.SEL
  N5: Part1.AIN1, Part2.HORZ
  N6: Part1.AIN0, Part2.VERT

notes:
  ADDR pin of ADS1115 has been grounded to get an I2C address of 0x48

custom parts:
  Adafruit ADS1115 16Bit I2C ADC: For microcontrollers without an analog-to-digital converter or when you want a higher-precision ADC, the ADS1115 provides 16-bit precision at 860 samples/second over I2C. The chip can be configured as 4 single-ended input channels, or two differential channels. As a nice bonus, it even includes a programmable gain amplifier, up to x16, to help boost up smaller single/differential signals to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
