# Fritzing sketch wiring (saved by Fritzing 0.9.3b)

parts:
  Part1 = SHT1x-Breakout
  WeMos_D1_Mini1 = WeMos D1 Mini
  Grove1 = Grove OLED 128x96

nets:
  VCC: Part1.VCC, WeMos_D1_Mini1.3V3
  N1: Part1.GND, WeMos_D1_Mini1.G
  N2: WeMos_D1_Mini1.D1, Grove1.SCL
  N3: WeMos_D1_Mini1.D2, Grove1.SDA
  N4: WeMos_D1_Mini1.D5, Grove1.VCC
